# Fritzing sketch Incubator (saved by Fritzing 0.9.3b)

parts:
  Часть1 = Arduino Uno (Rev3)
  DHT1 = DHT22 Humidity and Temperature Sensor
  Часть2 = LCD1602-I2C
  LED1 = LEDs [package=led10mm]
  Часть3 = Lilypad Battery Connect
  KY-1 = Keyes Relay [package=THT]
  LED2 = LED - 5mm [color="Red (633nm)" package="5 mm [THT]"]
  LED4 = LED - 5mm [color="Blue (525nm)" package="5 mm [THT]"]  # not connected
  R1 = Resistor [tolerance=±5% resistance=220 package=THT]
  R2 = Resistor [tolerance=±5% resistance=220 package=THT]
  J1 = Piezo Speaker
  PCB2 = RTC_DS1302_module
  hc-sr1 = hc-sr04

nets:
  N1: Часть1.A4/SDA, Часть2.SDA
  N2: Часть1.A5/SCL, Часть2.SCL
  N3: Часть1.D8, J1.pin2
  N4: Часть1.D10_PWM/SS, KY-1.signal
  N5: Часть1.D12/MISO, R2.Pin_1
  N6: Часть1.D13/SCK, R1.Pin_1
  GND: Часть1.GND, DHT1.GND, Часть2.GND, LED2.cathode
  N7: Часть1.D2, PCB2.RST
  N8: Часть1.D3_PWM, DHT1.DATA
  N9: Часть1.D4, PCB2.DAT
  N10: Часть1.D5_PWM, PCB2.CLK
  N11: Часть1.D6_PWM, hc-sr1.Echo
  N12: Часть1.D7, hc-sr1.Trig
  5V: Часть1.5V, Часть2.VCC
  N13: LED1.A, Часть3.-
  N14: LED1.C, KY-1.NO
  N15: Часть3.+, KY-1.C

notes:
  220V AC power
  led is responsible for the temperature
  led is responsible for the humidity

custom parts:
  LCD1602-I2C: A standard character display, usually with 2x16 characters. Comes in many colors with LCM1602 IIC attached.
  LEDs: LEDs Standard schematic elements and footprints for 5mm, 3mm, 1206, and 0603 sized LEDs. 5mm - Spark Fun Electronics SKU : COM-00529 (and others)
  Keyes Relay: The Keyes 5V relay module is suitable for SCM development, home appliance control. It uses a 5V~12V TIL control signal which can control DC / AC signal.
  RTC_DS1302_module: Arduino module DS1302 SPI Real Time Clock
